// Logisim project Digital State Machine- Group 9 - Works.circ as structural Verilog: 1 circuit, main circuit main
module main (
);

  wire and_1_out, and_2_out, and_3_out, and_4_out, and_5_out, and_6_out, and_7_out, and_8_out, and_9_out,
       and_10_out, and_11_out, and_12_out, and_13_out, and_14_out, and_15_out, and_16_out, and_17_out,
       and_18_out, and_19_out, and_20_out, and_21_out, and_22_out, and_23_out, and_24_out, and_25_out,
       and_26_out, and_27_out, and_28_out, and_29_out, and_30_out, and_31_out, and_32_out, and_33_out,
       clock_1_out, J1_out, J2_out, J3_out, J4_out, j_k_ff_1_q, j_k_ff_1_qn, j_k_ff_2_q, j_k_ff_2_qn,
       j_k_ff_3_q, j_k_ff_3_qn, j_k_ff_4_q, j_k_ff_4_qn, K1_out, K2_out, K3_out, K4_out, not_1_out,
       not_2_out, X1_out, X2_out, Z1_out, Z2_out, Z3_out, Z4_out, Z5_out, Z6_out, Z7_out, Z8_out, Z9_out,
       Z10_out, Z11_out, Z13_out;

  not not_1 (not_1_out, X1_out);
  not not_2 (not_2_out, X2_out);
  Button X2 (.out(X2_out));
  Button X1 (.out(X1_out));
  and and_1 (and_1_out, j_k_ff_2_q, not_1_out, not_2_out);
  and and_2 (and_2_out, j_k_ff_3_q, j_k_ff_4_q, not_1_out, not_2_out);
  and and_3 (and_3_out, j_k_ff_4_qn, X2_out);
  and and_4 (and_4_out, j_k_ff_1_qn, j_k_ff_4_q, X1_out);
  and and_5 (and_5_out, j_k_ff_3_qn, j_k_ff_4_q, X1_out);
  and and_6 (and_6_out, j_k_ff_1_qn, j_k_ff_3_q, X2_out);
  and and_7 (and_7_out, j_k_ff_1_q, not_1_out, not_2_out);
  and and_8 (and_8_out, j_k_ff_3_q, j_k_ff_4_q, not_1_out, X2_out);
  and and_9 (and_9_out, j_k_ff_1_qn, X2_out);
  and and_10 (and_10_out, j_k_ff_4_qn, X2_out);
  and and_11 (and_11_out, j_k_ff_1_qn, j_k_ff_4_q, X1_out);
  and and_12 (and_12_out, j_k_ff_1_q, j_k_ff_4_q, not_1_out, not_2_out);
  and and_13 (and_13_out, j_k_ff_2_qn, X1_out, not_2_out);
  and and_14 (and_14_out, j_k_ff_3_q, X1_out, not_2_out);
  and and_15 (and_15_out, j_k_ff_1_qn, j_k_ff_2_q, j_k_ff_3_qn, not_1_out, X2_out);
  and and_16 (and_16_out, j_k_ff_1_qn, X1_out);
  and and_17 (and_17_out, j_k_ff_3_qn, X1_out);
  and and_18 (and_18_out, j_k_ff_1_q, j_k_ff_3_q, not_1_out, not_2_out);
  and and_19 (and_19_out, j_k_ff_1_qn, j_k_ff_4_q, X2_out);
  and and_20 (and_20_out, j_k_ff_3_qn, j_k_ff_4_q, X2_out);
  and and_21 (and_21_out, j_k_ff_3_q, X2_out);
  and and_22 (and_22_out, j_k_ff_2_q, j_k_ff_3_qn, X1_out);
  and and_23 (and_23_out, j_k_ff_2_q, j_k_ff_4_q, X1_out);
  and and_24 (and_24_out, j_k_ff_3_qn, j_k_ff_4_q, X1_out);
  and and_25 (and_25_out, j_k_ff_2_qn, j_k_ff_4_qn, X2_out);
  or K2 (K2_out, and_7_out, and_8_out);
  and J3 (J3_out, j_k_ff_4_q, not_1_out, X2_out);
  or K3 (K3_out, and_9_out, and_10_out, and_11_out, and_12_out);
  or K1 (K1_out, and_1_out, and_2_out);
  or J2 (J2_out, and_3_out, and_4_out, and_5_out, and_6_out);
  or J1 (J1_out, and_21_out, and_22_out, and_23_out, and_24_out, and_25_out);
  Clock clock_1 (.out(clock_1_out));
  or J4 (J4_out, and_13_out, and_14_out, and_15_out);
  or K4 (K4_out, and_16_out, and_17_out, and_18_out, and_19_out, and_20_out);
  J_K_Flip_Flop j_k_ff_1 (
    .J(J1_out), .clk(clock_1_out), .K(K1_out), .Q(j_k_ff_1_q), .Qn(j_k_ff_1_qn));  // open: preset, en, reset
  J_K_Flip_Flop j_k_ff_2 (
    .J(J2_out), .clk(clock_1_out), .K(K2_out), .Q(j_k_ff_2_q), .Qn(j_k_ff_2_qn));  // open: preset, en, reset
  J_K_Flip_Flop j_k_ff_3 (
    .J(J3_out), .clk(clock_1_out), .K(K3_out), .Q(j_k_ff_3_q), .Qn(j_k_ff_3_qn));  // open: preset, en, reset
  J_K_Flip_Flop j_k_ff_4 (
    .J(J4_out), .clk(clock_1_out), .K(K4_out), .Q(j_k_ff_4_q), .Qn(j_k_ff_4_qn));  // open: preset, en, reset
  and and_26 (and_26_out, j_k_ff_1_qn, j_k_ff_2_q);
  and and_27 (and_27_out, j_k_ff_2_qn, j_k_ff_1_q);
  and and_28 (and_28_out, j_k_ff_3_q, j_k_ff_4_q);
  and and_29 (and_29_out, j_k_ff_2_q, j_k_ff_4_q);
  and and_30 (and_30_out, j_k_ff_2_q, j_k_ff_3_q);
  and and_31 (and_31_out, j_k_ff_2_q, j_k_ff_3_q, j_k_ff_4_q);
  and and_32 (and_32_out, j_k_ff_1_q, j_k_ff_4_q);
  and and_33 (and_33_out, j_k_ff_1_q, j_k_ff_3_q);
  or Z1 (Z1_out, and_26_out, and_27_out, j_k_ff_3_q, j_k_ff_4_q);
  or Z2 (Z2_out, and_26_out, and_27_out, j_k_ff_3_q);
  or Z3 (Z3_out, and_28_out, and_26_out, and_27_out);
  or Z4 (Z4_out, and_26_out, and_27_out);
  or Z5 (Z5_out, and_27_out, and_29_out, and_30_out);
  or Z6 (Z6_out, and_27_out, and_30_out);
  or Z7 (Z7_out, and_27_out, and_31_out);
  and Z8 (Z8_out, j_k_ff_1_q, j_k_ff_2_qn);
  or Z9 (Z9_out, and_32_out, and_33_out);
  and Z10 (Z10_out, j_k_ff_1_q, j_k_ff_3_q);
  and Z11 (Z11_out, j_k_ff_1_q, j_k_ff_3_q, j_k_ff_4_q);
  and Z13 (Z13_out, j_k_ff_1_q, j_k_ff_2_q);
  LED led_1 (.in(Z1_out));
  LED led_2 (.in(Z2_out));
  LED led_3 (.in(Z3_out));
  LED led_4 (.in(Z4_out));
  LED led_5 (.in(Z5_out));
  LED led_6 (.in(Z6_out));
  LED led_7 (.in(Z7_out));
  LED led_8 (.in(Z8_out));
  LED led_9 (.in(Z9_out));
  LED led_10 (.in(Z10_out));
  LED led_11 (.in(Z11_out));
  LED led_12 (.in(Z13_out));

  // Notes on the sheet:
  //   !X1
  //   Q1
  //   X2
  //   X1
  //   !x2
  //   Q4
  //   !Q
  //   Q3
  //   Q2
  //   1
  //   !Q
  //   !Q
  //   !Q
  //   2
  //   3
  //   4
endmodule
